# Fritzing sketch PCB_BackBox_2layers (saved by Fritzing 0.9.3b)
circuit board: 8.5cm x 5.5cm
breadboards: 1

parts:
  SONAR_1_(R) = Maxbotix MaxSonar Ultrasonic Sensor (Hi-Res)
  GAS_SENSOR_(IC1) = ADS1015 12-bit ADC Breakout
  SONAR_2_(L) = Maxbotix MaxSonar Ultrasonic Sensor (Hi-Res)
  ArduinoUNO = Arduino Uno (Rev3)
  SONAR_3_(Rear) = Maxbotix MaxSonar Ultrasonic Sensor (Hi-Res)
  USBTTL1 = USB TTL Serial Cable
  PM_SENSOR = female pin header, 4 pins [form="♀ (female)"]
  R1 = Resistor [tolerance=±5% resistance=1.2k package="0805 [SMD]"]
  LIDAR_(L) = LIDAR-Lite
  LIDAR_R = LIDAR-Lite

nets:
  GND: SONAR_1_(R).GND, GAS_SENSOR_(IC1).GND, SONAR_2_(L).GND, ArduinoUNO.GND, SONAR_3_(Rear).GND, USBTTL1.GND, PM_SENSOR.pin2, LIDAR_(L).GND, LIDAR_R.GND
  +5V: SONAR_1_(R).+5V, SONAR_1_(R).BW, GAS_SENSOR_(IC1).VDD, SONAR_2_(L).+5V, SONAR_2_(L).BW, ArduinoUNO.5V, SONAR_3_(Rear).+5V, SONAR_3_(Rear).BW, PM_SENSOR.pin1, LIDAR_(L).5V
  N1: SONAR_1_(R).RX, SONAR_3_(Rear).TX
  N2: SONAR_1_(R).AN, ArduinoUNO.A0
  N3: GAS_SENSOR_(IC1).SCL, ArduinoUNO.A5/SCL, LIDAR_(L).SCL
  N4: GAS_SENSOR_(IC1).SDA, ArduinoUNO.A4/SDA, LIDAR_(L).SDA
  N5: SONAR_2_(L).TX, SONAR_3_(Rear).RX
  N6: SONAR_2_(L).RX, ArduinoUNO.D13/SCK
  N7: SONAR_2_(L).AN, ArduinoUNO.A1
  N8: ArduinoUNO.A2, SONAR_3_(Rear).AN
  N9: ArduinoUNO.D10_PWM/SS, PM_SENSOR.pin3
  N10: ArduinoUNO.D11_PWM/MOSI, PM_SENSOR.pin4
  N11: ArduinoUNO.D12/MISO, R1.Pin_1
  N12: ArduinoUNO.D0/RX, USBTTL1.TX
  N13: ArduinoUNO.D1/TX, USBTTL1.RX
  N14: ArduinoUNO.D4, LIDAR_(L).PWR_EN
  N15: ArduinoUNO.RESET, R1.Pin_0

custom parts:
  Maxbotix MaxSonar Ultrasonic Sensor (Hi-Res): Maxbotix MaxSonar Hi-Resolution Ultrasonic Sensor HRLV-EZ0, HRLV-EZ1, HRLV-EZ2, HRLV-EZ3, HRLV-EZ4
  ADS1015 12-bit ADC Breakout: ADS1015 12-bit I2C ADC+PGA Breakout
  LIDAR-Lite: PulsedLight LIDAR-Lite Sensor
